// Logisim project mips-simulator.circ as structural Verilog: 6 circuits, main circuit Program_Counter
module Microprocessor (
  input  in_1,
  input  in_2
);

  wire alu_1_equal, and_1_out, clock_1_out, control_unit_1_out_2, control_unit_1_out_3, control_unit_1_out_4,
       control_unit_1_out_6, multiplexer_3_out, not_1_out, or_1_out;
  wire [1:0] control_unit_1_out_5, control_unit_1_out_7;
  wire [2:0] alu_control_unit_1_out_2;
  wire [3:0] demultiplexer_1_out0, demultiplexer_1_out1, multiplexer_4_out;
  wire [7:0] alu_1_out_9, alu_1_out_10;
  wire [15:0] adder_1_out, alu_1_out_4, multiplexer_1_out, multiplexer_2_out, multiplexer_5_out,
       multiplexer_6_out, program_counter_1_out_4, ram_2_data, register_file_1_out_7,
       register_file_1_read_data_2;
  wire [28:0] ram_1_data;

  Multiplexer #(.width(16), .enable("false")) multiplexer_1 (
    .in0(16'h1), .in1(ram_1_data[15:0]), .out(multiplexer_1_out), .sel(and_1_out));
  Multiplexer #(.select(2), .width(16), .enable("false")) multiplexer_2 (
    .in0(adder_1_out), .in1(ram_1_data[15:0]), .in2(register_file_1_out_7), .out(multiplexer_2_out),
    .sel(control_unit_1_out_5));  // open: in3
  Clock clock_1 (.out(clock_1_out));
  and and_1 (and_1_out, control_unit_1_out_3, multiplexer_3_out);
  Adder #(.width(16)) adder_1 (
    .a(multiplexer_1_out), .b(program_counter_1_out_4), .out(adder_1_out));  // open: cin, cout
  Program_Counter program_counter_1 (
    .in_1(multiplexer_2_out), .out_4(program_counter_1_out_4), .in_2(clock_1_out), .in_3(in_2));
  Multiplexer #(.enable("false")) multiplexer_3 (
    .in0(alu_1_equal), .in1(not_1_out), .out(multiplexer_3_out), .sel(control_unit_1_out_4));
  RAM #(.addrWidth(16), .dataWidth(29)) ram_1 (
    .addr(program_counter_1_out_4), .data(ram_1_data), .clk(clock_1_out));  // open: sel, ld, clr
  not not_1 (not_1_out, alu_1_equal);
  Demultiplexer #(.width(4), .enable("false")) demultiplexer_1 (
    .out0(demultiplexer_1_out0), .out1(demultiplexer_1_out1), .in(ram_1_data[23:20]), .sel(or_1_out));
  Multiplexer #(.width(4), .enable("false")) multiplexer_4 (
    .in0(ram_1_data[15:12]), .in1(demultiplexer_1_out1), .out(multiplexer_4_out), .sel(or_1_out));
  Control_Unit control_unit_1 (
    .in_1(ram_1_data[28:24]), .out_5(control_unit_1_out_5), .out_3(control_unit_1_out_3),
    .out_4(control_unit_1_out_4), .out_6(control_unit_1_out_6), .out_7(control_unit_1_out_7),
    .out_2(control_unit_1_out_2));
  or or_1 (or_1_out, control_unit_1_out_6, control_unit_1_out_3);
  ALU_Control_Unit alu_control_unit_1 (.in_1(ram_1_data[28:24]), .out_2(alu_control_unit_1_out_2));
  Register_File register_file_1 (
    .Read_register_1(ram_1_data[19:16]), .Read_register_2(multiplexer_4_out),
    .Write_register(demultiplexer_1_out0), .in_4(multiplexer_6_out), .Clock(clock_1_out),
    .out_7(register_file_1_out_7), .Read_data_2(register_file_1_read_data_2), .Clear(in_2));
  Multiplexer #(.width(16), .enable("false")) multiplexer_5 (
    .in0(register_file_1_read_data_2), .in1(ram_1_data[15:0]), .out(multiplexer_5_out),
    .sel(control_unit_1_out_2));
  ALU alu_1 (
    .in_2(register_file_1_out_7), .in_3(multiplexer_5_out), .out_4(alu_1_out_4), .Equal(alu_1_equal),
    .in_1(alu_control_unit_1_out_2), .out_9(alu_1_out_9), .out_10(alu_1_out_10));  // open: Zero, Carry, Overflow
  Multiplexer #(.select(2), .width(16), .enable("false")) multiplexer_6 (
    .in0(alu_1_out_4), .in1({alu_1_out_9, alu_1_out_10}), .in2(ram_2_data), .out(multiplexer_6_out),
    .sel(control_unit_1_out_7));  // open: in3
  RAM #(.addrWidth(16), .dataWidth(16), .bus("separate")) ram_2 (
    .addr(alu_1_out_4), .din(register_file_1_read_data_2), .data(ram_2_data), .str(control_unit_1_out_6),
    .clk(clock_1_out), .clr(in_1));  // open: sel, ld

  // Notes on the sheet:
  //   The MIPS 16-bit Microprocessor
  //   - Single cycle -
  //   Designed by: Bari BGF
  //   On: July 29th, 2023
  //   Last modified: Mar 8th, 2024
endmodule

module Program_Counter (
  input  [15:0] in_1,
  input  in_2,
  input  in_3,
  output [15:0] out_4
);

  Register #(.width(16)) register_1 (.D(in_1), .Q(out_4), .clk(in_2), .clr(in_3));  // open: en
endmodule

module Register_File (
  input  [3:0] Read_register_1,
  input  [3:0] Read_register_2,
  input  [3:0] Write_register,
  input  [15:0] in_4,
  input  Clock,
  input  Clear,
  output [15:0] out_7,
  output [15:0] Read_data_2
);

  wire demultiplexer_1_out0, demultiplexer_1_out1, demultiplexer_1_out2, demultiplexer_1_out3,
       demultiplexer_1_out4, demultiplexer_1_out5, demultiplexer_1_out6, demultiplexer_1_out7;
  wire [7:0] register_8_q, register_9_q;
  wire [15:0] bit_extender_1_out, bit_extender_2_out, register_1_q, register_2_q, register_3_q, register_4_q,
       register_5_q, register_6_q, register_7_q;

  Demultiplexer #(.select(4), .enable("false")) demultiplexer_1 (
    .out0(demultiplexer_1_out0), .out1(demultiplexer_1_out1), .out2(demultiplexer_1_out2),
    .out3(demultiplexer_1_out3), .out4(demultiplexer_1_out4), .out5(demultiplexer_1_out5),
    .out6(demultiplexer_1_out6), .out7(demultiplexer_1_out7), .in(1'b1), .sel(Write_register));  // open: out8, out9, out10, out11, out12, out13, out14, out15
  Register #(.width(16)) register_1 (.en(demultiplexer_1_out0), .Q(register_1_q), .clk(Clock), .clr(Clear));  // open: D
  Register #(.width(16)) register_2 (.D(in_4), .en(demultiplexer_1_out1), .Q(register_2_q), .clk(Clock), .clr(Clear));
  Register #(.width(16)) register_3 (.D(in_4), .en(demultiplexer_1_out2), .Q(register_3_q), .clk(Clock), .clr(Clear));
  Register #(.width(16)) register_4 (.D(in_4), .en(demultiplexer_1_out3), .Q(register_4_q), .clk(Clock), .clr(Clear));
  Register #(.width(16)) register_5 (.D(in_4), .en(demultiplexer_1_out4), .Q(register_5_q), .clk(Clock), .clr(Clear));
  Register #(.width(16)) register_6 (.D(in_4), .en(demultiplexer_1_out5), .Q(register_6_q), .clk(Clock), .clr(Clear));
  Register #(.width(16)) register_7 (.D(in_4), .en(demultiplexer_1_out6), .Q(register_7_q), .clk(Clock), .clr(Clear));
  Register register_8 (.D(in_4[7:0]), .en(demultiplexer_1_out7), .Q(register_8_q), .clk(Clock), .clr(Clear));
  Register register_9 (.D(in_4[15:8]), .en(demultiplexer_1_out7), .Q(register_9_q), .clk(Clock), .clr(Clear));
  assign bit_extender_1_out = {{8{1'b0}}, register_8_q};  // Bit_Extender bit_extender_1
  assign bit_extender_2_out = {{8{1'b0}}, register_9_q};  // Bit_Extender bit_extender_2
  Multiplexer #(.select(4), .width(16), .enable("false")) multiplexer_1 (
    .in0(register_1_q), .in1(register_2_q), .in2(register_3_q), .in3(register_4_q), .in4(register_5_q),
    .in5(register_6_q), .in6(register_7_q), .in7(bit_extender_1_out), .in8(bit_extender_2_out), .out(out_7),
    .sel(Read_register_1));  // open: in9, in10, in11, in12, in13, in14, in15
  Multiplexer #(.select(4), .width(16), .enable("false")) multiplexer_2 (
    .in0(register_1_q), .in1(register_2_q), .in2(register_3_q), .in3(register_4_q), .in4(register_5_q),
    .in5(register_6_q), .in6(register_7_q), .in7(bit_extender_1_out), .in8(bit_extender_2_out),
    .out(Read_data_2), .sel(Read_register_2));  // open: in9, in10, in11, in12, in13, in14, in15

  // Notes on the sheet:
  //   Write data
  //   zero
  //   rs
  //   rd
  //   t0
  //   t2
  //   lo
  //   hi
  //   t1
  //   t3
  //   Read data 1
endmodule

module ALU (
  input  [2:0] in_1,
  input  [15:0] in_2,
  input  [15:0] in_3,
  output [15:0] out_4,
  output Zero,
  output Carry,
  output Overflow,
  output Equal,
  output [7:0] out_9,
  output [7:0] out_10
);

  wire adder_1_cout, and_2_out, and_3_out, and_4_out, and_5_out, and_6_out, and_7_out, bitfinder_1_found,
       bitfinder_2_found, bitfinder_3_found, bitselector_1_out, bitselector_2_out, bitselector_3_out,
       bitselector_4_out, comparator_1_lt, comparator_3_eq, subtractor_1_bout, xnor_1_out, xor_2_out;
  wire [1:0] bit_extender_4_out;
  wire [15:0] adder_1_out, and_1_out, bit_extender_3_out, divider_1_out, divider_1_rem, multiplier_1_cout,
       multiplier_1_out, or_1_out, subtractor_1_out, xor_1_out;

  Adder #(.width(16)) adder_1 (.a(in_2), .b(in_3), .out(adder_1_out), .cout(adder_1_cout));  // open: cin
  Subtractor #(.width(16)) subtractor_1 (
    .a(in_2), .b(in_3), .out(subtractor_1_out), .bout(subtractor_1_bout));  // open: bin
  Multiplier #(.width(16)) multiplier_1 (
    .a(in_2), .b(in_3), .out(multiplier_1_out), .cout(multiplier_1_cout));  // open: cin
  assign and_1_out = in_2 & in_3;  // AND_Gate and_1, 16 bits wide
  assign or_1_out = in_2 | in_3;  // OR_Gate or_1, 16 bits wide
  assign xor_1_out = in_2 ^ in_3;  // XOR_Gate xor_1, 16 bits wide
  Divider #(.width(16)) divider_1 (.a(in_2), .b(in_3), .out(divider_1_out), .rem(divider_1_rem));  // open: upper
  Comparator #(.width(16)) comparator_1 (.a(in_2), .b(in_3), .eq(Equal), .lt(comparator_1_lt));  // open: gt
  Bit_Extender #(.in_width(16), .out_width(8)) bit_extender_1 (.in(divider_1_out), .out(out_9));
  Bit_Extender #(.in_width(16), .out_width(8)) bit_extender_2 (.in(divider_1_rem), .out(out_10));
  assign bit_extender_3_out = {{15{1'b0}}, comparator_1_lt};  // Bit_Extender bit_extender_3
  Multiplexer #(.select(3), .width(16), .enable("false")) multiplexer_1 (
    .in0(adder_1_out), .in1(subtractor_1_out), .in2(multiplier_1_out), .in3(and_1_out), .in4(or_1_out),
    .in5(xor_1_out), .in6(bit_extender_3_out), .out(out_4), .sel(in_1));  // open: in7
  Bit_Extender #(.in_width(3), .out_width(2)) bit_extender_4 (.in(in_1), .out(bit_extender_4_out));
  BitFinder #(.width(16)) bitfinder_1 (.in(multiplier_1_cout), .found(bitfinder_1_found));  // open: index
  BitSelector #(.width(16)) bitselector_1 (.in(in_2), .out(bitselector_1_out), .sel(4'b1111));
  BitSelector #(.width(16)) bitselector_2 (.in(in_3), .out(bitselector_2_out), .sel(4'b1111));
  Comparator #(.width(16)) comparator_2 (.a(out_4), .b({16{1'b0}}), .eq(Zero));  // open: gt, lt
  Multiplexer #(.select(2), .enable("false")) multiplexer_2 (
    .in1(adder_1_cout), .in2(subtractor_1_bout), .in3(bitfinder_1_found), .out(Carry),
    .sel(bit_extender_4_out));  // open: in0
  BitSelector #(.width(16)) bitselector_3 (.in(out_4), .out(bitselector_3_out), .sel(4'b1111));
  xnor xnor_1 (xnor_1_out, bitselector_1_out, bitselector_2_out);
  and and_2 (and_2_out, ~bitselector_2_out, bitselector_1_out);  // AND_Gate
  BitFinder #(.width(16)) bitfinder_2 (.in(in_2), .found(bitfinder_2_found));  // open: index
  and and_3 (and_3_out, bitfinder_2_found, bitfinder_3_found);
  BitFinder #(.width(16)) bitfinder_3 (.in(in_3), .found(bitfinder_3_found));  // open: index
  xor xor_2 (xor_2_out, bitselector_3_out, bitselector_2_out);
  and and_4 (and_4_out, ~bitselector_3_out, and_2_out);  // AND_Gate
  Comparator #(.width(3)) comparator_3 (.a(in_1), .b(3'b011), .eq(comparator_3_eq));  // open: gt, lt
  BitSelector #(.width(2)) bitselector_4 (.in(bit_extender_4_out), .out(bitselector_4_out), .sel(1'b0));
  and and_5 (and_5_out, xor_2_out, xnor_1_out);
  and and_6 (and_6_out, xnor_1_out, Zero, comparator_3_eq, and_3_out);
  and and_7 (and_7_out, bitselector_4_out, and_5_out);
  or or_2 (Overflow, and_7_out, and_4_out, and_6_out);

  // Notes on the sheet:
  //   Result
  //   Division Result
  //   Division Remainder
endmodule

module Control_Unit (
  input  [4:0] in_1,
  output out_2,
  output out_3,
  output out_4,
  output [1:0] out_5,
  output out_6,
  output [1:0] out_7
);

  wire demultiplexer_1_out4, demultiplexer_1_out5, demultiplexer_1_out6, demultiplexer_1_out7,
       demultiplexer_1_out8, demultiplexer_1_out12, demultiplexer_1_out13, demultiplexer_1_out14,
       demultiplexer_1_out15, demultiplexer_1_out16, demultiplexer_1_out17, demultiplexer_1_out19,
       demultiplexer_1_out21, demultiplexer_1_out22, nor_1_out, or_1_out, or_2_out;

  Demultiplexer #(.select(5), .enable("false")) demultiplexer_1 (
    .out4(demultiplexer_1_out4), .out5(demultiplexer_1_out5), .out6(demultiplexer_1_out6),
    .out7(demultiplexer_1_out7), .out8(demultiplexer_1_out8), .out12(demultiplexer_1_out12),
    .out13(demultiplexer_1_out13), .out14(demultiplexer_1_out14), .out15(demultiplexer_1_out15),
    .out16(demultiplexer_1_out16), .out17(demultiplexer_1_out17), .out18(out_6),
    .out19(demultiplexer_1_out19), .out20(out_4), .out21(demultiplexer_1_out21),
    .out22(demultiplexer_1_out22), .in(1'b1), .sel(in_1));  // open: out0, out1, out2, out3, out9, out10, out11, out23, out24, out25, out26, out27, out28, out29, out30, out31
  nor nor_1 (nor_1_out, demultiplexer_1_out22, demultiplexer_1_out21, out_4, demultiplexer_1_out19, out_6, demultiplexer_1_out8, demultiplexer_1_out4);
  or or_1 (or_1_out, demultiplexer_1_out4, demultiplexer_1_out8);
  or or_2 (or_2_out, demultiplexer_1_out15, demultiplexer_1_out16);
  or or_3 (out_2, demultiplexer_1_out5, demultiplexer_1_out6, demultiplexer_1_out7, demultiplexer_1_out8, demultiplexer_1_out12, demultiplexer_1_out13, demultiplexer_1_out14, demultiplexer_1_out16, demultiplexer_1_out17, out_6);
  or or_4 (out_3, demultiplexer_1_out19, out_4);
  Priority_Encoder #(.select(2), .disabled(0)) priority_encoder_1 (
    .in0(1'b1), .in1(demultiplexer_1_out22), .in2(demultiplexer_1_out21), .out(out_5));  // open: in3, gs, en_out, en_in
  Priority_Encoder #(.select(2), .disabled(0)) priority_encoder_2 (
    .in0(nor_1_out), .in1(or_1_out), .in2(demultiplexer_1_out17), .in3(or_2_out), .out(out_7));  // open: gs, en_out, en_in
endmodule

module ALU_Control_Unit (
  input  [4:0] in_1,
  output [2:0] out_2
);

  wire demultiplexer_1_out1, demultiplexer_1_out2, demultiplexer_1_out3, demultiplexer_1_out4,
       demultiplexer_1_out5, demultiplexer_1_out6, demultiplexer_1_out7, demultiplexer_1_out8,
       demultiplexer_1_out9, demultiplexer_1_out10, demultiplexer_1_out11, demultiplexer_1_out12,
       demultiplexer_1_out13, demultiplexer_1_out14, demultiplexer_1_out17, demultiplexer_1_out18, or_1_out,
       or_2_out, or_3_out, or_4_out, or_5_out, or_6_out, or_7_out;

  Demultiplexer #(.select(5), .enable("false")) demultiplexer_1 (
    .out1(demultiplexer_1_out1), .out2(demultiplexer_1_out2), .out3(demultiplexer_1_out3),
    .out4(demultiplexer_1_out4), .out5(demultiplexer_1_out5), .out6(demultiplexer_1_out6),
    .out7(demultiplexer_1_out7), .out8(demultiplexer_1_out8), .out9(demultiplexer_1_out9),
    .out10(demultiplexer_1_out10), .out11(demultiplexer_1_out11), .out12(demultiplexer_1_out12),
    .out13(demultiplexer_1_out13), .out14(demultiplexer_1_out14), .out17(demultiplexer_1_out17),
    .out18(demultiplexer_1_out18), .in(1'b1), .sel(in_1));  // open: out0, out15, out16, out19, out20, out21, out22, out23, out24, out25, out26, out27, out28, out29, out30, out31
  or or_1 (or_1_out, demultiplexer_1_out1, demultiplexer_1_out5, demultiplexer_1_out17, demultiplexer_1_out18);
  or or_2 (or_2_out, demultiplexer_1_out9, demultiplexer_1_out12);
  or or_3 (or_3_out, demultiplexer_1_out10, demultiplexer_1_out13);
  or or_4 (or_4_out, demultiplexer_1_out11, demultiplexer_1_out14);
  or or_5 (or_5_out, demultiplexer_1_out4, demultiplexer_1_out8);
  or or_6 (or_6_out, demultiplexer_1_out2, demultiplexer_1_out6);
  or or_7 (or_7_out, demultiplexer_1_out3, demultiplexer_1_out7);
  Priority_Encoder priority_encoder_1 (
    .in0(or_1_out), .in1(or_6_out), .in2(or_7_out), .in3(or_2_out), .in4(or_3_out), .in5(or_4_out),
    .in6(or_5_out), .out(out_2));  // open: in7, en_in, gs, en_out
endmodule
